// Logisim project project-5-gudbrand.circ as structural Verilog: 17 circuits, main circuit main
module main (
  input  [1:0] in_1,
  input  CLR
);

  wire CLK, control_unit_1_alusrc, control_unit_1_bl, control_unit_1_bx, control_unit_1_memtoreg,
       control_unit_1_memwrite, control_unit_1_pcsrc, control_unit_1_regwrite, finished_1_finished,
       program_finished_1_finished;
  wire [1:0] control_unit_1_immsrc, control_unit_1_regsrc;
  wire [2:0] control_unit_1_alucontrol;
  wire [3:0] alu_1_alu_flags, multiplexer_3_out, multiplexer_4_out, multiplexer_5_out;
  wire [31:0] adder_1_out, adder_2_out, alu_1_result, data_memory_1_rd, extend_1_extimm,
       instruction_memory_1_out_3, multiplexer_1_out, multiplexer_2_out, multiplexer_6_out,
       multiplexer_7_out, multiplexer_8_out, R0, R1, R2, R3, R4, R5, R6, R7, R8, R9, R10, R11, R12, R13, R14,
       register_1_q, register_file_1_rd1, register_file_1_rd2;

  LED led_1 (.in(program_finished_1_finished));
  // Probe on R0
  Clock u_CLK (.out(CLK));
  Multiplexer #(.width(32), .enable("false")) multiplexer_1 (
    .in0(multiplexer_8_out), .in1(register_file_1_rd2), .out(multiplexer_1_out), .sel(control_unit_1_bx));
  // Probe on R1
  Multiplexer #(.width(32), .enable("false")) multiplexer_2 (
    .in0(adder_1_out), .in1(multiplexer_1_out), .out(multiplexer_2_out), .sel(control_unit_1_pcsrc));
  // Probe on R2
  Program_Finished program_finished_1 (
    .A(register_1_q), .B(register_1_q), .Finished(program_finished_1_finished), .CLK(CLK), .CLR(CLR));
  Register #(.width(32)) register_1 (.D(multiplexer_2_out), .Q(register_1_q), .clk(CLK), .clr(CLR));  // open: en
  // Probe on R3
  // Probe on alu_1_alu_flags
  // Probe on instruction_memory_1_out_3
  Instruction_memory instruction_memory_1 (.A(register_1_q), .out_3(instruction_memory_1_out_3), .Program(in_1));
  Adder #(.width(32)) adder_1 (.a(register_1_q), .b(32'h4), .out(adder_1_out));  // open: cin, cout
  // Probe on R4
  // Probe on R5
  Finished finished_1 (.in_1(instruction_memory_1_out_3), .finished(finished_1_finished));
  LED led_2 (.in(finished_1_finished));
  Multiplexer #(.width(4), .enable("false")) multiplexer_3 (
    .in0(instruction_memory_1_out_3[19:16]), .in1(4'b1111), .out(multiplexer_3_out),
    .sel(control_unit_1_regsrc[0]));
  // Probe on R6
  Control_unit control_unit_1 (
    .Cond(instruction_memory_1_out_3[31:28]), .ALUFlags(alu_1_alu_flags),
    .Op(instruction_memory_1_out_3[27:26]), .Funct(instruction_memory_1_out_3[25:20]),
    .Rd(instruction_memory_1_out_3[15:12]), .PCSrc(control_unit_1_pcsrc), .RegWrite(control_unit_1_regwrite),
    .MemWrite(control_unit_1_memwrite), .MemtoReg(control_unit_1_memtoreg), .ALUSrc(control_unit_1_alusrc),
    .ImmSrc(control_unit_1_immsrc), .RegSrc(control_unit_1_regsrc), .ALUControl(control_unit_1_alucontrol),
    .CLK(CLK), .BL(control_unit_1_bl), .in_8(instruction_memory_1_out_3), .Bx(control_unit_1_bx), .CLR(CLR));
  Multiplexer #(.width(4), .enable("false")) multiplexer_4 (
    .in0(instruction_memory_1_out_3[3:0]), .in1(instruction_memory_1_out_3[15:12]), .out(multiplexer_4_out),
    .sel(control_unit_1_regsrc[1]));
  Adder #(.width(32)) adder_2 (.a(32'h4), .b(adder_1_out), .out(adder_2_out));  // open: cin, cout
  // Probe on R7
  // Probe on R8
  Multiplexer #(.width(4), .enable("false")) multiplexer_5 (
    .in0(instruction_memory_1_out_3[15:12]), .in1(4'b1110), .out(multiplexer_5_out), .sel(control_unit_1_bl));
  Multiplexer #(.width(32), .enable("false")) multiplexer_6 (
    .in0(multiplexer_8_out), .in1(adder_1_out), .out(multiplexer_6_out), .sel(control_unit_1_bl));
  // Probe on R9
  // Probe on R10
  // Probe on R11
  Register_file register_file_1 (
    .WE3(control_unit_1_regwrite), .CLK(CLK), .CLR(CLR), .A1(multiplexer_3_out), .A2(multiplexer_4_out),
    .A3(multiplexer_5_out), .WD3(multiplexer_6_out), .R15(adder_2_out), .RD1(register_file_1_rd1),
    .RD2(register_file_1_rd2), .R0(R0), .R1(R1), .R2(R2), .R3(R3), .R4(R4), .R5(R5), .R6(R6), .R7(R7),
    .R8(R8), .R9(R9), .R10(R10), .R11(R11), .R12(R12), .R13(R13), .R14(R14));
  // Probe on R12
  // Probe on R13
  Extend extend_1 (.Input(instruction_memory_1_out_3), .ExtImm(extend_1_extimm), .ImmSrc(control_unit_1_immsrc));
  // Probe on R14
  Multiplexer #(.width(32), .enable("false")) multiplexer_7 (
    .in0(register_file_1_rd2), .in1(extend_1_extimm), .out(multiplexer_7_out), .sel(control_unit_1_alusrc));
  ALU alu_1 (
    .ALUControl(control_unit_1_alucontrol), .B(multiplexer_7_out), .A(register_file_1_rd1),
    .Result(alu_1_result), .ALU_flags(alu_1_alu_flags));
  Data_Memory data_memory_1 (
    .ALURes(alu_1_result), .WD(register_file_1_rd2), .RD(data_memory_1_rd), .WE(control_unit_1_memwrite),
    .CLK(CLK), .CLR(CLR));
  Multiplexer #(.width(32), .enable("false")) multiplexer_8 (
    .in0(alu_1_result), .in1(data_memory_1_rd), .out(multiplexer_8_out), .sel(control_unit_1_memtoreg));

  // Other names for the same wires on the sheet: Prgm[1:0] = in_1

  // Notes on the sheet:
  //   PC'
  //   PC
  //   A
  //   RD
  //   Instruction
  //   Memory
  //   PCPlus4
  //   Instr
  //   PcSrc
  //   Control
  //   Unit
  //   Cond
  //   Op
  //   Funct
  //   Rd
  //   Flags
  //   BX
  //   RegSrc
  //   BL
  //   PCPlus8
  //   RA1
  //   RA2
  //   RegWrite
  //   WE3
  //   A1
  //   A2
  //   A3
  //   WD3
  //   R15
  //   Register
  //   File
  //   RD1
  //   RD2
  //   ImmSrc
  //   ALUSrc
  //   Extend
  //   ALUControl
  //   ExtImm
  //   SrcA
  //   SrcB
  //   WriteData
  //   ALUFlags
  //   ALUResult
  //   MemWrite
  //   WE
  //   A
  //   RD
  //   Data
  //   Memory
  //   WD
  //   MemtoReg
  //   ReadData
  //   Result
endmodule

// Zero
module AND_invert (
  input  [31:0] \input ,
  output out_2
);

  and and_1 (out_2, ~\input [0], ~\input [1], ~\input [2], ~\input [3], ~\input [4], ~\input [5], ~\input [6], ~\input [7], ~\input [8], ~\input [9], ~\input [10], ~\input [11], ~\input [12], ~\input [13], ~\input [14], ~\input [15], ~\input [16], ~\input [17], ~\input [18], ~\input [19], ~\input [20], ~\input [21], ~\input [22], ~\input [23], ~\input [24], ~\input [25], ~\input [26], ~\input [27], ~\input [28], ~\input [29], ~\input [30], ~\input [31]);  // AND_Gate
endmodule

module ALU (
  input  [2:0] ALUControl,
  input  [31:0] B,
  input  [31:0] A,
  output [31:0] Result,
  output [3:0] ALU_flags
);

  wire adder_1_cout, not_2_out, xnor_1_out, xor_1_out;
  wire [31:0] adder_1_out, and_1_out, multiplexer_1_out, not_1_out, or_1_out;

  // Probe on B
  // Probe on A
  assign not_1_out = ~B;  // NOT_Gate not_1, 32 bits wide
  Multiplexer #(.width(32), .enable("false")) multiplexer_1 (
    .in0(B), .in1(not_1_out), .out(multiplexer_1_out), .sel(ALUControl[0]));
  Adder #(.width(32)) adder_1 (
    .a(A), .b(multiplexer_1_out), .out(adder_1_out), .cin(ALUControl[0]), .cout(adder_1_cout));
  not not_2 (not_2_out, ALUControl[1]);
  xor xor_1 (xor_1_out, adder_1_out[31], A[31]);
  NotExactlyOne xnor_1 (.out(xnor_1_out), .in0(B[31]), .in1(A[31]), .in2(ALUControl[0]));
  assign and_1_out = B & A;  // AND_Gate and_1, 32 bits wide
  assign or_1_out = B | A;  // OR_Gate or_1, 32 bits wide
  Multiplexer #(.select(3), .width(32), .enable("false")) multiplexer_2 (
    .in0(adder_1_out), .in1(adder_1_out), .in2(and_1_out), .in3(or_1_out), .in4(B),
    .out({ALU_flags[3], Result[30:0]}), .sel(ALUControl));  // open: in5, in6, in7
  and and_2 (ALU_flags[1], adder_1_cout, not_2_out);
  and and_3 (ALU_flags[0], not_2_out, xor_1_out, xnor_1_out);
  AND_invert and_invert_1 (.\input ({ALU_flags[3], Result[30:0]}), .out_2(ALU_flags[2]));

  assign Result[31] = ALU_flags[3];

  // Notes on the sheet:
  //   B31
  //   A31
  //   ALUControl0
  //   Sum31
  //   A31
  //   ALUControl1
  //   Cout
  //   Sum
  //   Carry
  //   Overflow
  //   Zero
  //   Result31
  //   Negativ
  //   NZCV
endmodule

module Decoder (
  input  [3:0] rd,
  input  [1:0] Op,
  input  [5:0] Funct,
  output PCS,
  output RegW,
  output MemW,
  output MemtoReg,
  output ALUSrc,
  output [1:0] ImmSrc,
  output [1:0] RegSrc,
  output BL,
  output No_write,
  output [2:0] ALU_Control,
  output [1:0] Flag_W
);

  wire main_decoder_1_alu_op, main_decoder_1_branch;

  Main_decoder main_decoder_1 (
    .Op(Op), .Funct_5(Funct), .Branch(main_decoder_1_branch), .Mem_to_Reg(MemtoReg), .MemW(MemW),
    .ALU_src(ALUSrc), .Imm_Src(ImmSrc), .Reg_W(RegW), .Reg_Src(RegSrc), .ALU_op(main_decoder_1_alu_op),
    .BL(BL));
  ALU_decoder alu_decoder_1 (
    .ALUOp(main_decoder_1_alu_op), .in_2(Funct[4:0]), .ALU_control(ALU_Control), .No_Write(No_write),
    .Flag_W(Flag_W));
  Pc_logic pc_logic_1 (.Rd(rd), .Reg_W(RegW), .Branch(main_decoder_1_branch), .out_4(PCS));
endmodule

// ALU\n decoder
module ALU_decoder (
  input  ALUOp,
  input  [4:0] in_2,
  output [2:0] ALU_control,
  output No_Write,
  output [1:0] Flag_W
);

  wire Add_out, And_2_out, and_4_out, And_out, Or_2_out, or_5_out, or_6_out, Or_out, Sub_2_out, Sub_out;

  and Sub (Sub_out, ~in_2[1], in_2[2], ~in_2[3], ~in_2[4], ALUOp);  // AND_Gate
  and And (And_out, ~in_2[1], ~in_2[2], ~in_2[3], ~in_2[4], ALUOp);  // AND_Gate
  and Or (Or_out, ~in_2[1], ~in_2[2], in_2[3], in_2[4], ALUOp);  // AND_Gate
  and CMP (No_Write, in_2[0], in_2[4], ~in_2[3], in_2[2], ~in_2[1], ALUOp);  // AND_Gate
  and MOV (ALU_control[2], in_2[4], in_2[3], ~in_2[2], in_2[1], ~in_2[0]);  // AND_Gate
  and Add (Add_out, ~in_2[1], ~in_2[2], in_2[3], ~in_2[4], ALUOp);  // AND_Gate
  and Sub_2 (Sub_2_out, ~in_2[1], in_2[2], ~in_2[3], ~in_2[4], ALUOp);  // AND_Gate
  and Or_2 (Or_2_out, ~in_2[1], ~in_2[2], in_2[3], in_2[4], ALUOp);  // AND_Gate
  and And_2 (And_2_out, ~in_2[1], ~in_2[2], ~in_2[3], ~in_2[4], ALUOp);  // AND_Gate
  or or_3 (ALU_control[0], Sub_out, No_Write, Or_out);
  or or_4 (ALU_control[1], Or_out, And_out);
  or or_5 (or_5_out, Add_out, No_Write, Sub_2_out);
  or or_6 (or_6_out, Or_2_out, And_2_out);
  and and_3 (Flag_W[0], in_2[0], or_5_out);
  and and_4 (and_4_out, in_2[0], or_6_out);
  or or_7 (Flag_W[1], Flag_W[0], and_4_out);

  // Other names for the same wires on the sheet: func0 = in_2[0]
endmodule

module Main_decoder (
  input  [1:0] Op,
  input  [5:0] Funct_5,
  output Branch,
  output Mem_to_Reg,
  output MemW,
  output ALU_src,
  output [1:0] Imm_Src,
  output Reg_W,
  output [1:0] Reg_Src,
  output ALU_op,
  output BL
);

  wire and_1_out, and_2_out, or_5_out, or_9_out, or_10_out;
  wire [0:0] and_3_out, and_4_out;
  wire [1:0] or_3_out;
  wire [1:1] and_5_out, or_7_out;

  and and_1 (and_1_out, ~Op[0], ~Op[1], ~Funct_5[5]);  // AND_Gate
  and and_2 (and_2_out, ~Op[0], ~Op[1], Funct_5[5]);  // AND_Gate
  and and_3 (and_3_out[0], Op[0], ~Op[1], ~Funct_5[0]);  // AND_Gate
  and and_4 (and_4_out[0], Op[0], ~Op[1], Funct_5[0]);  // AND_Gate
  and and_5 (and_5_out[1], ~Op[0], Op[1]);  // AND_Gate
  nor nor_1 (Branch, and_1_out, and_2_out, and_3_out[0], and_4_out[0], ~and_5_out[1]);  // NOR_Gate
  nor nor_2 (Mem_to_Reg, and_1_out, and_2_out, and_3_out[0], ~and_4_out[0], and_5_out[1]);  // NOR_Gate
  nor nor_3 (MemW, and_1_out, and_2_out, ~and_3_out[0], and_4_out[0], and_5_out[1]);  // NOR_Gate
  or or_1 (ALU_src, ~and_1_out, and_2_out, and_3_out[0], and_4_out[0], and_5_out[1]);  // OR_Gate
  assign Imm_Src = or_3_out | {and_5_out[1], 1'b0};  // OR_Gate or_2, 2 bits wide
  assign or_3_out = {1'b0, and_3_out[0]} | {1'b0, and_4_out[0]};  // OR_Gate or_3, 2 bits wide
  or or_4 (Reg_W, and_1_out, and_2_out, and_4_out[0], ~or_5_out);  // OR_Gate
  or or_5 (or_5_out, and_3_out[0], and_5_out[1]);
  assign Reg_Src = {or_7_out[1], 1'b0} | {and_3_out[0], 1'b0} | {1'b0, and_5_out[1]};  // OR_Gate or_6, 2 bits wide
  or or_7 (or_7_out[1], and_2_out, and_4_out[0]);
  or or_8 (ALU_op, or_9_out, ~or_10_out);  // OR_Gate
  or or_9 (or_9_out, and_1_out, and_2_out);
  or or_10 (or_10_out, and_3_out[0], and_4_out[0], and_5_out[1]);
  and and_6 (BL, and_5_out[1], Funct_5[4]);
endmodule

module Pc_logic (
  input  [3:0] Rd,
  input  Reg_W,
  input  Branch,
  output out_4
);

  wire and_1_out;

  and and_1 (and_1_out, Rd[0], Rd[1], Rd[2], Rd[3], Reg_W);
  or or_1 (out_4, and_1_out, Branch);
endmodule

module Conditinal_Logic (
  input  PCS,
  input  RegW,
  input  No_write,
  input  MemW,
  input  CLR,
  input  [1:0] FlagW,
  input  [3:0] Cond,
  input  CLK,
  input  [3:0] ALUFlags,
  output PCSrc,
  output RegWrite,
  output MemWrite
);

  wire condition_check_1_condex;
  wire [1:0] and_1_out, bit_extender_1_out, register_1_q, register_2_q;

  Register #(.width(2)) register_1 (.D(ALUFlags[3:2]), .en(and_1_out[1]), .Q(register_1_q), .clk(CLK), .clr(CLR));
  Register #(.width(2)) register_2 (.D(ALUFlags[1:0]), .en(and_1_out[0]), .Q(register_2_q), .clk(CLK), .clr(CLR));
  assign bit_extender_1_out = {{1{condition_check_1_condex}}, condition_check_1_condex};  // Bit_Extender bit_extender_1
  assign and_1_out = FlagW & bit_extender_1_out;  // AND_Gate and_1, 2 bits wide
  Condition_check condition_check_1 (
    .CondEx(condition_check_1_condex), .Flags_2_3(register_1_q), .Flags_0_1(register_2_q), .Cond(Cond));
  and and_2 (PCSrc, PCS, condition_check_1_condex);
  and and_3 (RegWrite, RegW, ~No_write, condition_check_1_condex);  // AND_Gate
  and and_4 (MemWrite, MemW, condition_check_1_condex);

  // Notes on the sheet:
  //   Flags3:2
  //   Flags1:0
  //   [1]
  //   [0]
  //   CondEx
endmodule

module Condition_check (
  input  [1:0] Flags_2_3,
  input  [1:0] Flags_0_1,
  input  [3:0] Cond,
  output CondEx
);

  wire Allways_out, EQ_out, GT_out, LT_out, NE_out, or_1_out, xnor_1_out, xor_1_out;

  xor xor_1 (xor_1_out, Flags_0_1[0], Flags_2_3[1]);
  xnor xnor_1 (xnor_1_out, Flags_2_3[1], Flags_0_1[0]);
  or or_1 (or_1_out, Flags_2_3[0], xor_1_out);
  and Allways (Allways_out, Cond[3], Cond[2], Cond[1], ~Cond[0]);  // AND_Gate
  and EQ (EQ_out, ~Cond[3], ~Cond[2], ~Cond[1], ~Cond[0], Flags_2_3[0]);  // AND_Gate
  and NE (NE_out, ~Cond[3], ~Cond[2], ~Cond[1], Cond[0], ~Flags_2_3[0]);  // AND_Gate
  and LT (LT_out, Cond[3], Cond[2], ~Cond[1], Cond[0], or_1_out);  // AND_Gate
  and GT (GT_out, xnor_1_out, Cond[3], ~Cond[2], Cond[1], ~Cond[0]);  // AND_Gate
  or or_2 (CondEx, Allways_out, EQ_out, NE_out, LT_out, GT_out);
endmodule

module Control_unit (
  input  CLR,
  input  CLK,
  input  [3:0] Cond,
  input  [3:0] ALUFlags,
  input  [1:0] Op,
  input  [5:0] Funct,
  input  [3:0] Rd,
  input  [31:0] in_8,
  output PCSrc,
  output MemWrite,
  output RegWrite,
  output MemtoReg,
  output ALUSrc,
  output [1:0] ImmSrc,
  output [1:0] RegSrc,
  output [2:0] ALUControl,
  output BL,
  output Bx
);

  wire conditinal_logic_1_regwrite, decoder_1_memw, decoder_1_no_write, decoder_1_pcs, decoder_1_regw;
  wire [1:0] decoder_1_flag_w;

  Decoder decoder_1 (
    .rd(Rd), .Op(Op), .Funct(Funct), .PCS(decoder_1_pcs), .RegW(decoder_1_regw), .MemW(decoder_1_memw),
    .MemtoReg(MemtoReg), .ALUSrc(ALUSrc), .ImmSrc(ImmSrc), .RegSrc(RegSrc), .ALU_Control(ALUControl),
    .Flag_W(decoder_1_flag_w), .No_write(decoder_1_no_write), .BL(BL));
  BX_check bx_check_1 (.in_1(in_8), .BX(Bx));
  Conditinal_Logic conditinal_logic_1 (
    .PCS(decoder_1_pcs), .RegW(decoder_1_regw), .MemW(decoder_1_memw), .FlagW(decoder_1_flag_w), .Cond(Cond),
    .CLK(CLK), .ALUFlags(ALUFlags), .PCSrc(PCSrc), .RegWrite(conditinal_logic_1_regwrite),
    .MemWrite(MemWrite), .No_write(decoder_1_no_write), .CLR(CLR));
  or or_1 (RegWrite, conditinal_logic_1_regwrite, BL);
endmodule

module Data_Memory (
  input  [31:0] ALURes,
  input  [31:0] WD,
  input  WE,
  input  CLK,
  input  CLR,
  output [31:0] RD
);

  wire not_1_out;

  not not_1 (not_1_out, WE);
  RAM #(.addrWidth(10), .dataWidth(32), .bus("separate")) ram_1 (
    .addr(ALURes[9:0]), .din(WD), .data(RD), .str(WE), .clk(CLK), .ld(not_1_out), .clr(CLR));  // open: sel
endmodule

module Register_file (
  input  WE3,
  input  CLK,
  input  CLR,
  input  [3:0] A1,
  input  [3:0] A2,
  input  [3:0] A3,
  input  [31:0] WD3,
  input  [31:0] R15,
  output [31:0] R0,
  output [31:0] R1,
  output [31:0] R2,
  output [31:0] R3,
  output [31:0] R4,
  output [31:0] R5,
  output [31:0] R6,
  output [31:0] R7,
  output [31:0] R8,
  output [31:0] R9,
  output [31:0] R10,
  output [31:0] R11,
  output [31:0] R12,
  output [31:0] R13,
  output [31:0] R14,
  output [31:0] RD1,
  output [31:0] RD2
);

  wire and_1_out, and_2_out, and_3_out, and_4_out, and_5_out, and_6_out, and_7_out, and_8_out, and_9_out,
       and_10_out, and_11_out, and_12_out, and_13_out, and_14_out, and_15_out, decoder_1_out0,
       decoder_1_out1, decoder_1_out2, decoder_1_out3, decoder_1_out4, decoder_1_out5, decoder_1_out6,
       decoder_1_out7, decoder_1_out8, decoder_1_out9, decoder_1_out10, decoder_1_out11, decoder_1_out12,
       decoder_1_out13, decoder_1_out14;

  Decoder_part #(.select(4), .enable("false")) decoder_1 (
    .out0(decoder_1_out0), .out1(decoder_1_out1), .out2(decoder_1_out2), .out3(decoder_1_out3),
    .out4(decoder_1_out4), .out5(decoder_1_out5), .out6(decoder_1_out6), .out7(decoder_1_out7),
    .out8(decoder_1_out8), .out9(decoder_1_out9), .out10(decoder_1_out10), .out11(decoder_1_out11),
    .out12(decoder_1_out12), .out13(decoder_1_out13), .out14(decoder_1_out14), .sel(A3));  // open: out15
  and and_1 (and_1_out, WE3, decoder_1_out0);
  and and_2 (and_2_out, WE3, decoder_1_out1);
  and and_3 (and_3_out, WE3, decoder_1_out2);
  and and_4 (and_4_out, WE3, decoder_1_out3);
  and and_5 (and_5_out, WE3, decoder_1_out4);
  and and_6 (and_6_out, WE3, decoder_1_out5);
  and and_7 (and_7_out, WE3, decoder_1_out6);
  and and_8 (and_8_out, WE3, decoder_1_out7);
  and and_9 (and_9_out, WE3, decoder_1_out8);
  and and_10 (and_10_out, WE3, decoder_1_out9);
  and and_11 (and_11_out, WE3, decoder_1_out10);
  and and_12 (and_12_out, WE3, decoder_1_out11);
  and and_13 (and_13_out, WE3, decoder_1_out12);
  and and_14 (and_14_out, WE3, decoder_1_out13);
  and and_15 (and_15_out, WE3, decoder_1_out14);
  Register #(.width(32)) u_R0 (.D(WD3), .en(and_1_out), .Q(R0), .clk(CLK), .clr(CLR));
  Register #(.width(32)) u_R1 (.D(WD3), .en(and_2_out), .Q(R1), .clk(CLK), .clr(CLR));
  Register #(.width(32)) u_R2 (.D(WD3), .en(and_3_out), .Q(R2), .clk(CLK), .clr(CLR));
  Register #(.width(32)) u_R3 (.D(WD3), .en(and_4_out), .Q(R3), .clk(CLK), .clr(CLR));
  Register #(.width(32)) u_R4 (.D(WD3), .en(and_5_out), .Q(R4), .clk(CLK), .clr(CLR));
  Register #(.width(32)) u_R5 (.D(WD3), .en(and_6_out), .Q(R5), .clk(CLK), .clr(CLR));
  Register #(.width(32)) u_R6 (.D(WD3), .en(and_7_out), .Q(R6), .clk(CLK), .clr(CLR));
  Register #(.width(32)) u_R7 (.D(WD3), .en(and_8_out), .Q(R7), .clk(CLK), .clr(CLR));
  Register #(.width(32)) u_R8 (.D(WD3), .en(and_9_out), .Q(R8), .clk(CLK), .clr(CLR));
  Register #(.width(32)) u_R9 (.D(WD3), .en(and_10_out), .Q(R9), .clk(CLK), .clr(CLR));
  Register #(.width(32)) u_R10 (.D(WD3), .en(and_11_out), .Q(R10), .clk(CLK), .clr(CLR));
  Register #(.width(32)) u_R11 (.D(WD3), .en(and_12_out), .Q(R11), .clk(CLK), .clr(CLR));
  Register #(.width(32)) u_R12 (.D(WD3), .en(and_13_out), .Q(R12), .clk(CLK), .clr(CLR));
  Register #(.width(32)) u_R13 (.D(WD3), .en(and_14_out), .Q(R13), .clk(CLK), .clr(CLR));
  Register #(.width(32)) u_R14 (.D(WD3), .en(and_15_out), .Q(R14), .clk(CLK), .clr(CLR));
  Multiplexer #(.select(4), .width(32), .enable("false")) multiplexer_1 (
    .in0(R0), .in1(R1), .in2(R2), .in3(R3), .in4(R4), .in5(R5), .in6(R6), .in7(R7), .in8(R8), .in9(R9),
    .in10(R10), .in11(R11), .in12(R12), .in13(R13), .in14(R14), .in15(R15), .out(RD1), .sel(A1));
  Multiplexer #(.select(4), .width(32), .enable("false")) multiplexer_2 (
    .in0(R0), .in1(R1), .in2(R2), .in3(R3), .in4(R4), .in5(R5), .in6(R6), .in7(R7), .in8(R8), .in9(R9),
    .in10(R10), .in11(R11), .in12(R12), .in13(R13), .in14(R14), .in15(R15), .out(RD2), .sel(A2));
endmodule

module Instruction_memory (
  input  [1:0] Program,
  input  [31:0] A,
  output [31:0] out_3
);

  wire [31:0] rom_1_data, rom_2_data, rom_3_data, rom_4_data;

  ROM #(.dataWidth(32)) rom_1 (.addr(A[9:2]), .data(rom_1_data));  // open: sel
  ROM #(.dataWidth(32)) rom_2 (.addr(A[9:2]), .data(rom_2_data));  // open: sel
  ROM #(.dataWidth(32)) rom_3 (.addr(A[9:2]), .data(rom_3_data));  // open: sel
  ROM #(.dataWidth(32)) rom_4 (.addr(A[9:2]), .data(rom_4_data));  // open: sel
  Multiplexer #(.select(2), .width(32), .enable("false")) multiplexer_1 (
    .in0(rom_1_data), .in1(rom_2_data), .in2(rom_3_data), .in3(rom_4_data), .out(out_3), .sel(Program));

  // Notes on the sheet:
  //   sum_array_s(5,4,3,2,1)
  //   contents of rom_1 (hex, n*v repeats v):
  //   e3a0d080 e08dd00d e08dd00d e08dd00d e24dd004 e3a00005 e58d0000 e24dd004 e3a00004 e58d0000 e24dd004
  //   e3a00003 e58d0000 e24dd004 e3a00002 e58d0000 e24dd004 e3a00001 e58d0000 e1a0000d e3a01005 eb000000
  //   eafffffe e3a02000 e3a03000 e1530001 a000004 e590c000 e082200c e2833001 e2800004 eafffff8 e1a00002
  //   e12fff1e 1541 61656100 1006962 b 1080206
  //   find_max_s(3,6,4,7,1,5)
  //   contents of rom_2 (hex, n*v repeats v):
  //   e3a0d080 e08dd00d e08dd00d e08dd00d e24dd004 e3a00003 e58d0000 e24dd004 e3a00006 e58d0000 e24dd004
  //   e3a00004 e58d0000 e24dd004 e3a00007 e58d0000 e24dd004 e3a00001 e58d0000 e1a0000d e3a01005 eb000000
  //   eafffffe e5902000 e3a03001 e1530001 aa000005 e590c000 e15c0002 a1a0200c e2833001 e2800004 eafffff7
  //   e1a00002 e28dd014 e12fff1e
  //   fib_iter_s(12)
  //   contents of rom_3 (hex, n*v repeats v):
  //   e3a0000c e3a0d0c8 eb000000 eafffffe e3500001 ba000010 e24dd008 e58d4000 e58d5004 e3a01000 e3a02001
  //   e3a03001 e3a04000 e1530000 aa000004 e0824001 e2833001 e1a01002 e1a02004 eafffff8 e1a00004 e28dd008
  //   e12fff1e e3a00001 e12fff1e
  //   fib_rec_s(12)
  //   contents of rom_4 (hex, n*v repeats v):
  //   e3a0000c e3a0d080 e08dd00d e08dd00d e08dd00d eb000000 eafffffe e24dd010 e58de000 e3500000 1a000001
  //   e3a00000 ea00000d e3500001 1a000001 e3a00001 ea000009 e58d0004 e2400001 ebfffff2 e1a01000 e58d1008
  //   e59d0004 e2400002 ebffffed e59d1008 e0810000 e59de000 e28dd010 e12fff1e
endmodule

module Extend (
  input  [31:0] Input,
  input  [1:0] ImmSrc,
  output [31:0] ExtImm
);

  wire [31:0] bit_extender_1_out, bit_extender_2_out, bit_extender_3_out, shifter_1_out;

  assign bit_extender_1_out = {{24{1'b0}}, Input[7:0]};  // Bit_Extender bit_extender_1
  assign bit_extender_2_out = {{20{1'b0}}, Input[11:0]};  // Bit_Extender bit_extender_2
  assign bit_extender_3_out = {{8{Input[23]}}, Input[23:0]};  // Bit_Extender bit_extender_3
  Shifter #(.width(32)) shifter_1 (.in(bit_extender_3_out), .\dist (5'b00010), .out(shifter_1_out));
  Multiplexer #(.select(2), .width(32), .enable("false")) multiplexer_1 (
    .in0(bit_extender_1_out), .in1(bit_extender_2_out), .in2(shifter_1_out), .out(ExtImm), .sel(ImmSrc));  // open: in3
endmodule

// Bx\ncheck
module BX_check (
  input  [31:0] in_1,
  output BX
);

  Comparator #(.width(24)) comparator_1 (.a(in_1[27:4]), .b(24'h12fff1), .eq(BX));  // open: gt, lt
endmodule

// Finished
module Program_Finished (
  input  CLK,
  input  CLR,
  input  [31:0] A,
  input  [31:0] B,
  output Finished
);

  wire and_invert_1_out_2, subtractor_1_bout;
  wire [31:0] register_1_q, subtractor_1_out;

  Register #(.width(32)) register_1 (.D(A), .Q(register_1_q), .clk(CLK), .clr(CLR));  // open: en
  Subtractor #(.width(32)) subtractor_1 (
    .a(register_1_q), .b(B), .out(subtractor_1_out), .bout(subtractor_1_bout));  // open: bin
  AND_invert and_invert_1 (.\input (subtractor_1_out), .out_2(and_invert_1_out_2));
  and and_1 (Finished, and_invert_1_out_2, ~subtractor_1_bout);  // AND_Gate
endmodule

module Finished (
  input  [31:0] in_1,
  output finished
);

  Comparator #(.width(32)) comparator_1 (.a(in_1), .b(32'heafffffe), .eq(finished));  // open: gt, lt
endmodule
